// Logisim project Ex1.circ as structural Verilog: 1 circuit, main circuit main
module main (
  input  in_1,
  input  in_2,
  output Sum,
  output Carry
);

  xor XOR (Sum, in_1, in_2);
  and AND (Carry, in_1, in_2);
endmodule
