// Logisim project Ex2.circ as structural Verilog: 1 circuit, main circuit main
module main (
  input  a,
  input  b,
  input  c_in,
  output Sum,
  output Carry
);

  wire AND_2_out, AND_out, XOR_out;

  xor XOR (XOR_out, a, b);
  and AND (AND_out, a, b);
  and AND_2 (AND_2_out, XOR_out, c_in);
  xor XOR_2 (Sum, XOR_out, c_in);
  or OR (Carry, AND_2_out, AND_out);
endmodule
