// Logisim project Ex3.circ as structural Verilog: 2 circuits, main circuit 1b_full_adder
module _1b_full_adder (
  input  a,
  input  b,
  input  c_in,
  output Sum,
  output Carry
);

  wire AND_2_out, AND_out, XOR_out;

  xor XOR (XOR_out, a, b);
  and AND (AND_out, a, b);
  and AND_2 (AND_2_out, XOR_out, c_in);
  xor XOR_2 (Sum, XOR_out, c_in);
  or OR (Carry, AND_2_out, AND_out);
endmodule

module main (
  input  [7:0] a,
  input  [7:0] b,
  output [7:0] Sum,
  output Carry
);

  wire n1b_full_adder_1_carry, n1b_full_adder_2_carry, n1b_full_adder_3_carry, n1b_full_adder_4_carry,
       n1b_full_adder_5_carry, n1b_full_adder_6_carry, n1b_full_adder_7_carry;

  _1b_full_adder u_1b_full_adder_1 (.a(a[0]), .b(b[0]), .c_in(1'b0), .Sum(Sum[0]), .Carry(n1b_full_adder_1_carry));
  _1b_full_adder u_1b_full_adder_2 (
    .a(a[1]), .b(b[1]), .c_in(n1b_full_adder_1_carry), .Sum(Sum[1]), .Carry(n1b_full_adder_2_carry));
  _1b_full_adder u_1b_full_adder_3 (
    .a(a[2]), .b(b[2]), .c_in(n1b_full_adder_2_carry), .Sum(Sum[2]), .Carry(n1b_full_adder_3_carry));
  _1b_full_adder u_1b_full_adder_4 (
    .a(a[3]), .b(b[3]), .c_in(n1b_full_adder_3_carry), .Sum(Sum[3]), .Carry(n1b_full_adder_4_carry));
  _1b_full_adder u_1b_full_adder_5 (
    .a(a[4]), .b(b[4]), .c_in(n1b_full_adder_4_carry), .Sum(Sum[4]), .Carry(n1b_full_adder_5_carry));
  _1b_full_adder u_1b_full_adder_6 (
    .a(a[5]), .b(b[5]), .c_in(n1b_full_adder_5_carry), .Sum(Sum[5]), .Carry(n1b_full_adder_6_carry));
  _1b_full_adder u_1b_full_adder_7 (
    .a(a[6]), .b(b[6]), .c_in(n1b_full_adder_6_carry), .Sum(Sum[6]), .Carry(n1b_full_adder_7_carry));
  _1b_full_adder u_1b_full_adder_8 (.a(a[7]), .b(b[7]), .c_in(n1b_full_adder_7_carry), .Sum(Sum[7]), .Carry(Carry));

  // Notes on the sheet:
  //   Sum: pull=down
endmodule
