// Logisim project Ex1.circ as structural Verilog: 1 circuit, main circuit main
module main (
  input  W,
  input  X,
  input  Y,
  input  Z,
  output out_5
);

  wire and_1_out, and_2_out, and_3_out, and_4_out, and_5_out, and_6_out, and_7_out, and_8_out, or_1_out,
       or_2_out;

  and and_1 (and_1_out, X, ~Y, Z);  // AND_Gate
  and and_2 (and_2_out, ~X, ~Y, Z);  // AND_Gate
  and and_3 (and_3_out, ~W, X, Y);  // AND_Gate
  and and_4 (and_4_out, W, ~X, Y);  // AND_Gate
  and and_5 (and_5_out, W, X, Y);
  and and_6 (and_6_out, ~Y, Z);  // AND_Gate
  and and_7 (and_7_out, X, Y);
  and and_8 (and_8_out, W, Y);
  or or_1 (or_1_out, and_1_out, and_2_out, and_3_out, and_4_out, and_5_out);
  or or_2 (or_2_out, and_6_out, and_7_out, and_8_out);
  xnor xnor_1 (out_5, or_1_out, or_2_out);
endmodule
