// Logisim project Ex2.circ as structural Verilog: 2 circuits, main circuit main
module main (
  input  [1:0] A,
  input  [1:0] B,
  output [3:0] M
);

  wire and_2_out, and_3_out, and_4_out, and_5_out, and_6_out, and_7_out, and_8_out, and_9_out, and_10_out;

  and and_1 (M[0], A[0], B[0]);
  and and_2 (and_2_out, A[0], B[1]);
  and and_3 (and_3_out, A[1], B[0]);
  and and_4 (and_4_out, A[0], B[1]);
  and and_5 (and_5_out, A[1], B[0]);
  and and_6 (and_6_out, A[0], B[1]);
  and and_7 (and_7_out, B[0], A[1]);
  and and_8 (and_8_out, and_4_out, and_5_out);
  and and_9 (and_9_out, A[1], B[1]);
  and and_10 (and_10_out, and_6_out, and_7_out);
  xor xor_1 (M[1], and_2_out, and_3_out);
  xor xor_2 (M[2], and_8_out, and_9_out);
  and and_11 (M[3], and_9_out, and_10_out);
endmodule

module Half_Adder (
  input  in_1,
  input  in_2,
  output Sum,
  output Carry
);

  xor XOR (Sum, in_1, in_2);
  and AND (Carry, in_1, in_2);
endmodule
