// Logisim project Ex3.circ as structural Verilog: 3 circuits, main circuit main
module main (
  input  [2:0] A,
  input  [1:0] B,
  output [4:0] out_3
);

  wire and_2_out, and_3_out, and_4_out, and_5_out, and_6_out, full_adder_1_carry, half_adder_1_carry;

  and and_1 (out_3[0], A[0], B[0]);
  and and_2 (and_2_out, A[1], B[0]);
  and and_3 (and_3_out, A[0], B[1]);
  and and_4 (and_4_out, B[0], A[2]);
  and and_5 (and_5_out, A[1], B[1]);
  and and_6 (and_6_out, A[2], B[1]);
  Half_adder half_adder_1 (.in_1(and_2_out), .in_2(and_3_out), .Sum(out_3[1]), .Carry(half_adder_1_carry));
  full_adder full_adder_1 (
    .a(half_adder_1_carry), .b(and_4_out), .c_in(and_5_out), .Sum(out_3[2]), .Carry(full_adder_1_carry));
  Half_adder half_adder_2 (.in_1(full_adder_1_carry), .in_2(and_6_out), .Sum(out_3[3]), .Carry(out_3[4]));
endmodule

module Half_adder (
  input  in_1,
  input  in_2,
  output Sum,
  output Carry
);

  xor XOR (Sum, in_1, in_2);
  and AND (Carry, in_1, in_2);
endmodule

module full_adder (
  input  a,
  input  b,
  input  c_in,
  output Sum,
  output Carry
);

  wire AND_2_out, AND_out, XOR_out;

  xor XOR (XOR_out, a, b);
  and AND (AND_out, a, b);
  and AND_2 (AND_2_out, XOR_out, c_in);
  xor XOR_2 (Sum, XOR_out, c_in);
  or OR (Carry, AND_2_out, AND_out);
endmodule
