// Logisim project Lab4_Ex1.circ as structural Verilog: 10 circuits, main circuit main
module main (
  input  [3:0] A,
  input  [3:0] B,
  input  [2:0] S,
  output Overflow,
  output Sign,
  output [3:0] F,
  output C_out
);

  wire and_1_out, and_2_out, and_4_out, and_5_out, nand_1_out, not_1_out, not_2_out, not_3_out, not_4_out,
       not_5_out, not_6_out, or_1_out, to_bcd_1_a, to_bcd_1_b, to_bcd_1_c, to_bcd_1_d, to_bcd_1_e,
       to_bcd_1_f, to_bcd_1_g;
  wire [3:0] adder_1_out, AND_3_out_3, multiplexer_1_out, n1s_comp_1_out_3, n2s_comp_enable_1_out, OR_2_out,
       XNOR_out, XOR_out;

  and and_1 (and_1_out, S[1], not_1_out);
  _2s_comp_enable u_2s_comp_enable_1 (.Enable(or_1_out), .A(B), .C_in(and_1_out), .Out(n2s_comp_enable_1_out));
  not not_1 (not_1_out, S[0]);
  nand nand_1 (nand_1_out, S[0], not_2_out);
  not not_2 (not_2_out, S[1]);
  _1s_comp u_1s_comp_1 (.A(A), .C_in(and_2_out), .out_3(n1s_comp_1_out_3));
  and and_2 (and_2_out, S[1], S[0]);
  or or_1 (or_1_out, S[0], S[1]);
  AND AND_3 (.A(A), .B(B), .out_3(AND_3_out_3));
  OR OR_2 (.A(A), .B(B), .Out(OR_2_out));
  XOR XOR (.A(A), .B(B), .Out(XOR_out));
  XNOR XNOR (.A(A), .B(B), .Out(XNOR_out));
  Adder #(.width(4)) adder_1 (
    .a(n1s_comp_1_out_3), .b(n2s_comp_enable_1_out), .out(adder_1_out), .cin(nand_1_out), .cout(C_out));
  Multiplexer #(.select(2), .width(4)) multiplexer_1 (
    .in0(AND_3_out_3), .in1(OR_2_out), .in2(XOR_out), .in3(XNOR_out), .out(multiplexer_1_out), .sel(S[1:0]),
    .en(not_3_out));
  not not_3 (not_3_out, S[2]);
  not not_4 (not_4_out, adder_1_out[3]);
  not not_5 (not_5_out, B[3]);
  not not_6 (not_6_out, A[3]);
  Multiplexer #(.width(4), .enable("false")) multiplexer_2 (
    .in0(multiplexer_1_out), .in1(adder_1_out), .out(F), .sel(S[2]));
  and and_4 (and_4_out, A[3], B[3], not_4_out);
  or or_3 (Overflow, and_4_out, and_5_out);
  and and_5 (and_5_out, not_5_out, not_6_out, adder_1_out[3]);
  To_BCD to_bcd_1 (
    .in_1(adder_1_out), .a(to_bcd_1_a), .b(to_bcd_1_b), .c(to_bcd_1_c), .d(to_bcd_1_d), .e(to_bcd_1_e),
    .f(to_bcd_1_f), .g(to_bcd_1_g));
  _7_Segment_Display u_7_segment_display_1 (
    .g(to_bcd_1_g), .f(to_bcd_1_f), .a(to_bcd_1_a), .b(to_bcd_1_b), .e(to_bcd_1_e), .d(to_bcd_1_d),
    .c(to_bcd_1_c));  // open: dp

  assign Sign = F[3];
endmodule

module AND (
  input  [3:0] A,
  input  [3:0] B,
  output [3:0] out_3
);

  and and_1 (out_3[0], A[0], B[0]);
  and and_2 (out_3[1], A[1], B[1]);
  and and_3 (out_3[2], A[2], B[2]);
  and and_4 (out_3[3], A[3], B[3]);
endmodule

module OR (
  input  [3:0] A,
  input  [3:0] B,
  output [3:0] Out
);

  or or_1 (Out[0], A[0], B[0]);
  or or_2 (Out[1], A[1], B[1]);
  or or_3 (Out[2], A[2], B[2]);
  or or_4 (Out[3], A[3], B[3]);
endmodule

module XOR (
  input  [3:0] A,
  input  [3:0] B,
  output [3:0] Out
);

  xor xor_1 (Out[0], A[0], B[0]);
  xor xor_2 (Out[1], A[1], B[1]);
  xor xor_3 (Out[2], A[2], B[2]);
  xor xor_4 (Out[3], A[3], B[3]);
endmodule

module XNOR (
  input  [3:0] A,
  input  [3:0] B,
  output [3:0] Out
);

  xnor xnor_1 (Out[0], A[0], B[0]);
  xnor xnor_2 (Out[1], A[1], B[1]);
  xnor xnor_3 (Out[2], A[2], B[2]);
  xnor xnor_4 (Out[3], A[3], B[3]);
endmodule

module _1b_full_adder (
  input  a,
  input  b,
  input  c_in,
  output Sum,
  output Carry
);

  wire AND_2_out, AND_out, XOR_out;

  xor XOR (XOR_out, a, b);
  and AND (AND_out, a, b);
  and AND_2 (AND_2_out, XOR_out, c_in);
  xor XOR_2 (Sum, XOR_out, c_in);
  or OR (Carry, AND_2_out, AND_out);
endmodule

module _4b_full_adder (
  input  C_in,
  input  [3:0] A,
  input  [3:0] B,
  output [3:0] Sum,
  output out_5,
  output out_6
);

  wire n1b_full_adder_1_carry, n1b_full_adder_2_carry, n1b_full_adder_3_carry;

  _1b_full_adder u_1b_full_adder_1 (.a(C_in), .b(A[0]), .c_in(B[0]), .Sum(Sum[0]), .Carry(n1b_full_adder_1_carry));
  _1b_full_adder u_1b_full_adder_2 (
    .a(n1b_full_adder_1_carry), .b(A[1]), .c_in(B[1]), .Sum(Sum[1]), .Carry(n1b_full_adder_2_carry));
  _1b_full_adder u_1b_full_adder_3 (
    .a(n1b_full_adder_2_carry), .b(A[2]), .c_in(B[2]), .Sum(Sum[2]), .Carry(n1b_full_adder_3_carry));
  _1b_full_adder u_1b_full_adder_4 (.a(n1b_full_adder_3_carry), .b(B[3]), .c_in(A[3]), .Sum(Sum[3]), .Carry(out_5));
  xor xor_1 (out_6, Sum[3], out_5);

  // Notes on the sheet:
  //   C_in: pull=down
endmodule

module To_BCD (
  input  [3:0] in_1,
  output a,
  output b,
  output c,
  output d,
  output e,
  output f,
  output g
);

  wire and_1_out, and_2_out, and_3_out, and_4_out, and_5_out, and_6_out, and_7_out, and_8_out, and_9_out,
       and_10_out, and_11_out, and_12_out, and_13_out, and_14_out, and_15_out, and_16_out, not_1_out,
       not_2_out, not_3_out, not_4_out, not_5_out, not_6_out, not_7_out, not_8_out, not_9_out, not_10_out,
       not_11_out, not_12_out, not_13_out, not_14_out, not_15_out, not_16_out, not_17_out, not_18_out,
       not_19_out, not_20_out, not_21_out;

  not not_1 (not_1_out, in_1[2]);
  not not_2 (not_2_out, in_1[0]);
  not not_3 (not_3_out, in_1[1]);
  not not_4 (not_4_out, in_1[0]);
  not not_5 (not_5_out, in_1[1]);
  not not_6 (not_6_out, in_1[2]);
  not not_7 (not_7_out, in_1[0]);
  not not_8 (not_8_out, in_1[2]);
  not not_9 (not_9_out, in_1[0]);
  not not_10 (not_10_out, in_1[1]);
  not not_11 (not_11_out, in_1[2]);
  not not_12 (not_12_out, in_1[0]);
  not not_13 (not_13_out, in_1[0]);
  not not_14 (not_14_out, in_1[1]);
  not not_15 (not_15_out, in_1[0]);
  not not_16 (not_16_out, in_1[1]);
  not not_17 (not_17_out, in_1[0]);
  not not_18 (not_18_out, in_1[2]);
  not not_19 (not_19_out, in_1[1]);
  not not_20 (not_20_out, in_1[0]);
  and and_1 (and_1_out, not_1_out, not_2_out);
  and and_2 (and_2_out, in_1[2], in_1[0]);
  not not_21 (not_21_out, in_1[2]);
  and and_3 (and_3_out, not_3_out, not_4_out);
  and and_4 (and_4_out, in_1[1], in_1[0]);
  or or_1 (c, not_5_out, in_1[0], in_1[2]);
  and and_5 (and_5_out, not_6_out, not_7_out);
  and and_6 (and_6_out, not_8_out, in_1[1]);
  and and_7 (and_7_out, in_1[1], not_9_out);
  and and_8 (and_8_out, in_1[2], not_10_out, in_1[0]);
  and and_9 (and_9_out, not_11_out, not_12_out);
  and and_10 (and_10_out, in_1[1], not_13_out);
  and and_11 (and_11_out, not_14_out, not_15_out);
  and and_12 (and_12_out, in_1[2], not_16_out);
  and and_13 (and_13_out, in_1[2], not_17_out);
  and and_14 (and_14_out, not_18_out, in_1[1]);
  and and_15 (and_15_out, in_1[2], not_19_out);
  and and_16 (and_16_out, in_1[2], not_20_out);
  or or_2 (a, and_1_out, in_1[1], and_2_out, in_1[3]);
  or or_3 (b, not_21_out, and_3_out, and_4_out);
  or or_4 (d, and_5_out, and_6_out, and_7_out, and_8_out, in_1[3]);
  or or_5 (e, and_9_out, and_10_out);
  or or_6 (f, and_11_out, and_12_out, and_13_out, in_1[3]);
  or or_7 (g, and_14_out, and_15_out, and_16_out, in_1[3]);
  _7_Segment_Display u_7_segment_display_1 (.g(g), .f(f), .a(a), .b(b), .e(e), .d(d), .c(c));  // open: dp
endmodule

module _2s_comp_enable (
  input  Enable,
  input  [3:0] A,
  input  C_in,
  output [3:0] Out
);

  wire [3:0] xor_1_out;

  xor xor_1 (xor_1_out[0], A[0], C_in);
  xor xor_2 (xor_1_out[1], A[1], C_in);
  xor xor_3 (xor_1_out[2], A[2], C_in);
  xor xor_4 (xor_1_out[3], A[3], C_in);
  assign Out = {4{Enable}} & xor_1_out;  // AND_Gate and_1, 4 bits wide
endmodule

module _1s_comp (
  input  [3:0] A,
  input  C_in,
  output [3:0] out_3
);

  xor xor_1 (out_3[0], A[0], C_in);
  xor xor_2 (out_3[1], A[1], C_in);
  xor xor_3 (out_3[2], A[2], C_in);
  xor xor_4 (out_3[3], A[3], C_in);
endmodule
