// Logisim project lab5_ex1.circ as structural Verilog: 2 circuits, main circuit main
module main (
  input  in_1,
  output [3:0] out_2
);

  wire and_1_out, and_2_out, and_3_out, and_4_out, and_5_out, and_6_out, not_1_out, not_2_out, not_3_out,
       or_1_out, or_2_out, or_3_out, to_bcd_1_a, to_bcd_1_b, to_bcd_1_c, to_bcd_1_d, to_bcd_1_e, to_bcd_1_f,
       to_bcd_1_g;

  not not_1 (not_1_out, out_2[0]);
  not not_2 (not_2_out, out_2[1]);
  not not_3 (not_3_out, out_2[2]);
  and and_1 (and_1_out, out_2[2], not_2_out);
  or or_1 (or_1_out, and_1_out, and_2_out);
  and and_2 (and_2_out, not_3_out, out_2[1], out_2[0]);
  and and_3 (and_3_out, not_2_out, out_2[0]);
  or or_2 (or_2_out, and_3_out, and_4_out);
  and and_4 (and_4_out, not_3_out, out_2[1], not_1_out);
  and and_5 (and_5_out, not_2_out, not_1_out);
  or or_3 (or_3_out, and_5_out, and_6_out);
  and and_6 (and_6_out, not_3_out, out_2[1], not_1_out);
  D_Flip_Flop A (.clk(in_1), .D(or_1_out), .Q(out_2[2]));  // open: Qn, preset, en, reset
  D_Flip_Flop B (.clk(in_1), .D(or_2_out), .Q(out_2[1]));  // open: Qn, preset, en, reset
  D_Flip_Flop C (.clk(in_1), .D(or_3_out), .Q(out_2[0]));  // open: Qn, preset, en, reset
  Pull_Resistor pull_resistor_1 (.node(out_2[3]));
  To_BCD to_bcd_1 (
    .in_1(out_2), .a(to_bcd_1_a), .b(to_bcd_1_b), .c(to_bcd_1_c), .d(to_bcd_1_d), .e(to_bcd_1_e),
    .f(to_bcd_1_f), .g(to_bcd_1_g));
  _7_Segment_Display u_7_segment_display_1 (
    .g(to_bcd_1_g), .f(to_bcd_1_f), .a(to_bcd_1_a), .b(to_bcd_1_b), .e(to_bcd_1_e), .d(to_bcd_1_d),
    .c(to_bcd_1_c));  // open: dp
endmodule

module To_BCD (
  input  [3:0] in_1,
  output a,
  output b,
  output c,
  output d,
  output e,
  output f,
  output g
);

  wire and_1_out, and_2_out, and_3_out, and_4_out, and_5_out, and_6_out, and_7_out, and_8_out, and_9_out,
       and_10_out, and_11_out, and_12_out, and_13_out, and_14_out, and_15_out, and_16_out, not_1_out,
       not_2_out, not_3_out, not_4_out, not_5_out, not_6_out, not_7_out, not_8_out, not_9_out, not_10_out,
       not_11_out, not_12_out, not_13_out, not_14_out, not_15_out, not_16_out, not_17_out, not_18_out,
       not_19_out, not_20_out, not_21_out;

  not not_1 (not_1_out, in_1[2]);
  not not_2 (not_2_out, in_1[0]);
  not not_3 (not_3_out, in_1[1]);
  not not_4 (not_4_out, in_1[0]);
  not not_5 (not_5_out, in_1[1]);
  not not_6 (not_6_out, in_1[2]);
  not not_7 (not_7_out, in_1[0]);
  not not_8 (not_8_out, in_1[2]);
  not not_9 (not_9_out, in_1[0]);
  not not_10 (not_10_out, in_1[1]);
  not not_11 (not_11_out, in_1[2]);
  not not_12 (not_12_out, in_1[0]);
  not not_13 (not_13_out, in_1[0]);
  not not_14 (not_14_out, in_1[1]);
  not not_15 (not_15_out, in_1[0]);
  not not_16 (not_16_out, in_1[1]);
  not not_17 (not_17_out, in_1[0]);
  not not_18 (not_18_out, in_1[2]);
  not not_19 (not_19_out, in_1[1]);
  not not_20 (not_20_out, in_1[0]);
  and and_1 (and_1_out, not_1_out, not_2_out);
  and and_2 (and_2_out, in_1[2], in_1[0]);
  not not_21 (not_21_out, in_1[2]);
  and and_3 (and_3_out, not_3_out, not_4_out);
  and and_4 (and_4_out, in_1[1], in_1[0]);
  or or_1 (c, not_5_out, in_1[0], in_1[2]);
  and and_5 (and_5_out, not_6_out, not_7_out);
  and and_6 (and_6_out, not_8_out, in_1[1]);
  and and_7 (and_7_out, in_1[1], not_9_out);
  and and_8 (and_8_out, in_1[2], not_10_out, in_1[0]);
  and and_9 (and_9_out, not_11_out, not_12_out);
  and and_10 (and_10_out, in_1[1], not_13_out);
  and and_11 (and_11_out, not_14_out, not_15_out);
  and and_12 (and_12_out, in_1[2], not_16_out);
  and and_13 (and_13_out, in_1[2], not_17_out);
  and and_14 (and_14_out, not_18_out, in_1[1]);
  and and_15 (and_15_out, in_1[2], not_19_out);
  and and_16 (and_16_out, in_1[2], not_20_out);
  or or_2 (a, and_1_out, in_1[1], and_2_out, in_1[3]);
  or or_3 (b, not_21_out, and_3_out, and_4_out);
  or or_4 (d, and_5_out, and_6_out, and_7_out, and_8_out, in_1[3]);
  or or_5 (e, and_9_out, and_10_out);
  or or_6 (f, and_11_out, and_12_out, and_13_out, in_1[3]);
  or or_7 (g, and_14_out, and_15_out, and_16_out, in_1[3]);
  _7_Segment_Display u_7_segment_display_1 (.g(g), .f(f), .a(a), .b(b), .e(e), .d(d), .c(c));  // open: dp
endmodule
