// Logisim project lab5_ex2.circ as structural Verilog: 1 circuit, main circuit main
module main (
  input  in_1,
  output out_2
);

  wire and_1_out, and_2_out, and_3_out, button_1_out, d_ff_1_q, d_ff_1_qn, d_ff_2_q, d_ff_2_qn, not_1_out,
       or_1_out;

  Button button_1 (.out(button_1_out));
  not not_1 (not_1_out, in_1);
  and and_1 (and_1_out, d_ff_1_qn, in_1);
  and and_2 (and_2_out, d_ff_2_qn, in_1);
  and and_3 (and_3_out, d_ff_2_q, d_ff_1_qn, not_1_out);
  or or_1 (or_1_out, and_1_out, and_2_out);
  and and_4 (out_2, d_ff_1_q, d_ff_2_qn, in_1);
  D_Flip_Flop d_ff_1 (.clk(button_1_out), .D(and_3_out), .Q(d_ff_1_q), .Qn(d_ff_1_qn));  // open: preset, en, reset
  D_Flip_Flop d_ff_2 (.clk(button_1_out), .D(or_1_out), .Q(d_ff_2_q), .Qn(d_ff_2_qn));  // open: preset, en, reset
endmodule
